# Fritzing sketch SensorCircuit (saved by Fritzing 0.9.4)
breadboards: 1

parts:
  R1 = Resistor [tolerance=±5% resistance=220 package=THT]
  LED1 = LED - 5mm [color="Red (633nm)" package="5 mm [THT]"]
  J1 = Piezo Speaker
  Parça1 = Arduino Nano 33 BLE Sense
  PIR1 = PIR sensor

nets:
  N1: R1.Pin_0, Parça1.D10~
  N2: R1.Pin_1, LED1.anode
  GND: LED1.cathode, J1.pin1, Parça1.GND, Parça1.A7, PIR1.GND
  N3: J1.pin2, Parça1.D3~
  N4: Parça1.D2, PIR1.SIG
  +5V: Parça1.D11/MOSI, Parça1.+5V, PIR1.VDD

custom parts:
  Arduino Nano 33 BLE Sense: The Nano 33 BLE Sense (without headers) is Arduino’s 3.3V AI enabled board in the smallest available form factor: 45x18mm! The Arduino Nano 33 BLE Sense is a completely new board on a well-known form factor. It comes with a series of embedded sensors: 9 axis inertial sensor: what makes this board ideal for wearable devices humidity, and temperature sensor: to get highly accurate measurements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
